# Fritzing sketch Simon (saved by Fritzing 0.6.5b)
breadboards: 1

parts:
  LED1 = LED - 5mm [color="Red (633nm)" package="5 mm [THT]"]
  LED2 = LED - 5mm [color="Blue (525nm)" package="5 mm [THT]"]
  LED3 = LED - 5mm [color="Yellow (595nm)" package="5 mm [THT]"]
  LED4 = LED - 5mm [color="Green (570nm)" package="5 mm [THT]"]
  J1 = Piezo Speaker
  R1 = Resistor [tolerance=±5% resistance=2.2k package=THT]
  R2 = Resistor [tolerance=±5% resistance=2.2k package=THT]
  R3 = Resistor [tolerance=±5% resistance=2.2k package=THT]
  R4 = Resistor [tolerance=±5% resistance=560 package=THT]
  Arduino1 = Arduino
  S1 = Pushbutton [package="[THT]"]
  S2 = Pushbutton [package="[THT]"]
  S3 = Pushbutton [package="[THT]"]
  S4 = Pushbutton [package="[THT]"]

nets:
  N1: LED1.cathode, R1.Pin_1
  N2: LED1.anode, Arduino1.D1TX
  N3: LED2.cathode, R2.Pin_1
  N4: LED2.anode, Arduino1.D2
  N5: LED3.cathode, R4.Pin_1
  N6: LED3.anode, Arduino1.D3
  N7: LED4.cathode, R3.Pin_1
  N8: LED4.anode, Arduino1.D4
  N9: J1.pin1, R1.Pin_0, R2.Pin_0, R3.Pin_0, R4.Pin_0, Arduino1.GND, S1.Pin_1, S1.Pin_2, S2.Pin_1, S2.Pin_2, S3.Pin_1, S3.Pin_2, S4.Pin_1, S4.Pin_2
  N10: J1.pin2, Arduino1.D5
  N11: Arduino1.D12, S1.Pin_3, S1.Pin_4
  N12: Arduino1.D11, S2.Pin_3, S2.Pin_4
  N13: Arduino1.D10, S3.Pin_3, S3.Pin_4
  N14: Arduino1.D9, S4.Pin_3, S4.Pin_4
